// Logisim project cu.circ as structural Verilog: 1 circuit, main circuit main
module main (
  input  ST,
  input  Z,
  input  RS,
  output Y1,
  output Y2,
  output Y3,
  output Y4,
  output Y5,
  output Y7
);

  wire G_out, Q0_q, Q0_qn, Q1_q, Q1_qn, Q2_q, Q2_qn, T0_2_out, T0_3_out, T0_out, T1_2_out, T1_3_out,
       T1_4_out, T1_5_out, T1_out, T2_2_out, T2_3_out, T2_4_out, T2_5_out, T2_out, Y4_3_out, Y4_out;

  Clock #(.highDuration(2), .lowDuration(2)) G (.out(G_out));
  T_Flip_Flop #(.trigger("falling")) Q2 (
    .clk(G_out), .T(T2_3_out), .Q(Q2_q), .Qn(Q2_qn), .reset(RS), .en(1'b1));  // open: preset
  T_Flip_Flop #(.trigger("falling")) Q1 (
    .clk(G_out), .T(T1_5_out), .Q(Q1_q), .Qn(Q1_qn), .reset(RS), .en(1'b1));  // open: preset
  T_Flip_Flop #(.trigger("falling")) Q0 (
    .clk(G_out), .T(T0_2_out), .Q(Q0_q), .Qn(Q0_qn), .reset(RS), .en(1'b1));  // open: preset
  and T0 (T0_out, Q2_q, Q1_q, Q0_qn);
  nor T0_2 (T0_2_out, T0_out, T0_3_out);
  and T0_3 (T0_3_out, ~ST, Q2_qn, Q1_qn, Q0_qn);  // AND_Gate
  and T1 (T1_out, ~Z, Q1_qn);  // AND_Gate
  and T1_2 (T1_2_out, Z, Q2_qn);
  or T1_3 (T1_3_out, T1_out, T1_2_out, T1_4_out);
  and T1_4 (T1_4_out, Q2_qn, Q1_qn);
  and T2 (T2_out, Z, Q2_q, Q1_qn, Q0_qn);
  and T2_2 (T2_2_out, Q2_qn, Q1_q, Q0_q);
  or T2_3 (T2_3_out, T2_out, T2_2_out, T2_4_out, T2_5_out);
  and T2_4 (T2_4_out, Q2_q, Q1_q, Q0_qn);
  and T2_5 (T2_5_out, ~Z, Q1_q, Q0_qn);  // AND_Gate
  and u_Y1 (Y1, Q0_q, Q1_qn, Q2_qn);
  and u_Y2 (Y2, Q0_q, Q1_qn);
  and u_Y3 (Y3, Q0_qn, Q1_q, Q2_qn);
  and u_Y4 (Y4_out, Q0_q, Q1_q, Q2_qn);
  or Y4_2 (Y4, Y4_out, Y4_3_out);
  and Y4_3 (Y4_3_out, Q0_qn, Q1_q, Q2_q);
  and u_Y5 (Y5, Q0_q, Q1_q, Q2_qn);
  and u_Y7 (Y7, Q0_qn, Q1_q, Q2_q);
  nand T1_5 (T1_5_out, Q0_qn, T1_3_out);
endmodule
