// Logisim project od.circ as structural Verilog: 1 circuit, main circuit main
module main (
  input  [6:0] X,
  input  W_RG2,
  input  SL_RG2,
  input  W_CT,
  input  plus_1_CT,
  input  [6:0] Y,
  input  W_RG3,
  input  W_RG1,
  input  SL_RG1,
  input  R_RG1,
  output [13:0] Z
);

  wire and_1_out, G_out, RG2_out;
  wire [2:0] CT_q;
  wire [6:0] RG3_q;
  wire [13:0] adder_1_out, bit_extender_1_out;

  Clock #(.highDuration(2), .lowDuration(2)) G (.out(G_out));
  Shift_Register #(.length(7), .trigger("falling")) RG2 (
    .shift(SL_RG2), .in(W_RG3), .clk(G_out), .out(RG2_out), .load(W_RG2), .d0(X[0]), .d1(X[1]), .d2(X[2]),
    .d3(X[3]), .d4(X[4]), .d5(X[5]), .d6(X[6]));  // open: clr, q0, q1, q2, q3, q4, q5, q6
  Shift_Register #(.length(14), .trigger("falling")) RG1 (
    .shift(SL_RG1), .in(W_RG3), .clk(G_out), .load(W_RG1), .clr(R_RG1), .d0(adder_1_out[0]), .q0(Z[0]),
    .d1(adder_1_out[1]), .q1(Z[1]), .d2(adder_1_out[2]), .q2(Z[2]), .d3(adder_1_out[3]), .q3(Z[3]),
    .d4(adder_1_out[4]), .q4(Z[4]), .d5(adder_1_out[5]), .q5(Z[5]), .d6(adder_1_out[6]), .q6(Z[6]),
    .d7(adder_1_out[7]), .q7(Z[7]), .d8(adder_1_out[8]), .q8(Z[8]), .d9(adder_1_out[9]), .q9(Z[9]),
    .d10(adder_1_out[10]), .q10(Z[10]), .d11(adder_1_out[11]), .q11(Z[11]), .d12(adder_1_out[12]),
    .q12(Z[12]), .d13(adder_1_out[13]), .q13(Z[13]));  // open: out
  Counter #(.width(3), .max('h7), .ongoal("stay"), .trigger("falling")) CT (
    .load(W_CT), .D(3'b001), .count(plus_1_CT), .Q(CT_q), .clk(G_out));  // open: carry, clr
  Register #(.width(7), .trigger("falling")) RG3 (.D(Y), .en(W_RG3), .Q(RG3_q), .clk(G_out));  // open: clr
  // Probe on and_1_out
  // Probe on RG2_out
  and and_1 (and_1_out, CT_q[0], CT_q[1], CT_q[2]);
  assign bit_extender_1_out = {{7{1'b0}}, RG3_q};  // Bit_Extender bit_extender_1
  Adder #(.width(14)) adder_1 (.a(bit_extender_1_out), .b(Z), .out(adder_1_out));  // open: cin, cout
  // also tied to GND on the sheet: W_RG3
endmodule
