// Logisim project lab1.circ as structural Verilog: 1 circuit, main circuit main
module main (
  input  ST,
  input  RS,
  input  [3:0] C,
  input  [3:0] A,
  input  [3:0] B,
  output Z,
  output FN,
  output Y1,
  output W_C,
  output Y2,
  output Y3,
  output W_D,
  output SR_C,
  output Y4,
  output W_A,
  output Y5,
  output R_D,
  output Y7,
  output W_B,
  output plus_1_B,
  output minus_1_B
);

  wire G_out, not_1_out, or_1_out, or_2_out, Q0_q, Q0_qn, Q1_q, Q1_qn, Q2_q, Q2_qn, T0_2_out, T0_3_out,
       T0_out, T1_2_out, T1_3_out, T1_4_out, T1_5_out, T1_out, T2_2_out, T2_3_out, T2_4_out, T2_5_out,
       T2_out, Y4_2_out, Y4_out;
  wire [3:0] adder_1_out, multiplexer_1_out, RGA_q, RGB_q, RGC_q3, RGD_q;

  Clock #(.highDuration(2), .lowDuration(2)) G (.out(G_out));
  T_Flip_Flop #(.trigger("falling")) Q2 (
    .clk(G_out), .T(T2_5_out), .Q(Q2_q), .Qn(Q2_qn), .reset(RS), .en(1'b1));  // open: preset
  T_Flip_Flop #(.trigger("falling")) Q1 (
    .clk(G_out), .T(T1_5_out), .Q(Q1_q), .Qn(Q1_qn), .reset(RS), .en(1'b1));  // open: preset
  T_Flip_Flop #(.trigger("falling")) Q0 (
    .clk(G_out), .T(T0_3_out), .Q(Q0_q), .Qn(Q0_qn), .reset(RS), .en(1'b1));  // open: preset
  and T0 (T0_out, Q2_q, Q1_q, Q0_qn);
  and T0_2 (T0_2_out, ~ST, Q2_qn, Q1_qn, Q0_qn);  // AND_Gate
  and T1 (T1_out, ~Z, Q1_qn);  // AND_Gate
  and T1_2 (T1_2_out, Z, Q2_qn);
  and T1_3 (T1_3_out, Q2_qn, Q1_qn);
  and T2 (T2_out, Z, Q2_q, Q1_qn, Q0_qn);
  and T2_2 (T2_2_out, Q2_qn, Q1_q, Q0_q);
  and T2_3 (T2_3_out, Q2_q, Q1_q, Q0_qn);
  and T2_4 (T2_4_out, ~Z, Q1_q, Q0_qn);  // AND_Gate
  and u_Y1 (R_D, Q0_q, Q1_qn, Q2_qn);
  and u_Y2 (W_A, Q0_q, Q1_qn);
  and u_Y3 (plus_1_B, Q0_qn, Q1_q, Q2_qn);
  and u_Y4 (Y4_out, Q0_q, Q1_q, Q2_qn);
  and Y4_2 (Y4_2_out, Q0_qn, Q1_q, Q2_q);
  and u_Y5 (minus_1_B, Q0_q, Q1_q, Q2_qn);
  and u_Y7 (FN, Q0_qn, Q1_q, Q2_q);
  nor T0_3 (T0_3_out, T0_out, T0_2_out);
  or T1_4 (T1_4_out, T1_out, T1_2_out, T1_3_out);
  or T2_5 (T2_5_out, T2_out, T2_2_out, T2_3_out, T2_4_out);
  or Y4_3 (W_D, Y4_out, Y4_2_out);
  nand T1_5 (T1_5_out, Q0_qn, T1_4_out);
  or or_1 (or_1_out, R_D, minus_1_B);
  or or_2 (or_2_out, plus_1_B, minus_1_B);
  Shift_Register #(.length(4), .trigger("falling")) RGC (
    .shift(plus_1_B), .in(1'b0), .clk(G_out), .load(R_D), .d0(C[3]), .q0(RGC_q3[3]), .d1(C[2]),
    .q1(RGC_q3[2]), .d2(C[1]), .q2(RGC_q3[1]), .d3(C[0]), .q3(RGC_q3[0]));  // open: out, clr
  not not_1 (not_1_out, R_D);
  Counter #(.width(4), .max('hf), .ongoal("stay"), .trigger("falling")) RGB (
    .load(or_1_out), .D(B), .count(or_2_out), .Q(RGB_q), .clk(G_out));  // open: carry, clr
  Multiplexer #(.width(4), .enable("false")) multiplexer_1 (
    .in0(A), .in1(RGC_q3), .out(multiplexer_1_out), .sel(not_1_out));
  Register #(.width(4), .trigger("falling")) RGA (
    .D(multiplexer_1_out), .en(W_A), .Q(RGA_q), .clk(G_out));  // open: clr
  or or_3 (Z, RGB_q[0], RGB_q[1], RGB_q[2], RGB_q[3]);
  Adder #(.width(4)) adder_1 (.a(RGD_q), .b(RGA_q), .out(adder_1_out));  // open: cin, cout
  Register #(.width(4), .trigger("falling")) RGD (.D(adder_1_out), .en(W_D), .Q(RGD_q), .clk(G_out), .clr(R_D));
  // Probe on RGD_q
  // Probe on Z

  assign SR_C = plus_1_B;
  assign W_B = R_D;
  assign W_C = R_D;
  assign Y1 = R_D;
  assign Y2 = W_A;
  assign Y3 = plus_1_B;
  assign Y4 = W_D;
  assign Y5 = minus_1_B;
  assign Y7 = FN;

  // Notes on the sheet:
  //   SM
endmodule
