// Logisim project od.circ as structural Verilog: 1 circuit, main circuit main
module main (
  input  [3:0] C,
  input  W_C,
  input  [3:0] A,
  input  W_D,
  input  SR_C,
  input  W_A,
  input  R_D,
  input  [3:0] B,
  input  W_B,
  input  plus_1_B,
  input  minus_1_B
);

  wire G_out, not_1_out, or_1_out, or_2_out, or_3_out;
  wire [3:0] adder_1_out, multiplexer_1_out, RGA_q, RGB_q, RGC_q3, RGD_q;

  Clock #(.highDuration(2), .lowDuration(2)) G (.out(G_out));
  or or_1 (or_1_out, W_B, minus_1_B);
  or or_2 (or_2_out, plus_1_B, minus_1_B);
  Shift_Register #(.length(4), .trigger("falling")) RGC (
    .shift(SR_C), .in(1'b0), .clk(G_out), .load(W_C), .d0(C[3]), .q0(RGC_q3[3]), .d1(C[2]), .q1(RGC_q3[2]),
    .d2(C[1]), .q2(RGC_q3[1]), .d3(C[0]), .q3(RGC_q3[0]));  // open: out, clr
  not not_1 (not_1_out, R_D);
  Counter #(.width(4), .max('hf), .ongoal("stay"), .trigger("falling")) RGB (
    .load(or_1_out), .D(B), .count(or_2_out), .Q(RGB_q), .clk(G_out));  // open: carry, clr
  Multiplexer #(.width(4), .enable("false")) multiplexer_1 (
    .in0(A), .in1(RGC_q3), .out(multiplexer_1_out), .sel(not_1_out));
  Register #(.width(4), .trigger("falling")) RGA (
    .D(multiplexer_1_out), .en(W_A), .Q(RGA_q), .clk(G_out));  // open: clr
  or or_3 (or_3_out, RGB_q[0], RGB_q[1], RGB_q[2], RGB_q[3]);
  Adder #(.width(4)) adder_1 (.a(RGD_q), .b(RGA_q), .out(adder_1_out));  // open: cin, cout
  Register #(.width(4), .trigger("falling")) RGD (.D(adder_1_out), .en(W_D), .Q(RGD_q), .clk(G_out), .clr(R_D));
  // Probe on RGD_q
  // Probe on or_3_out

  // Notes on the sheet:
  //   SM
endmodule
