// Logisim project lab1.circ as structural Verilog: 1 circuit, main circuit Lab1
module Lab1 (
);

  wire CT_carry, RG2_out;
  wire [3:0] RG3_q;
  wire [4:0] bit_extender_1_out;
  wire [8:0] adder_1_out, RG1_q0;

  assign bit_extender_1_out = {{4{1'b0}}, 1'b0};  // Bit_Extender bit_extender_1
  Register #(.width(4), .trigger("falling")) RG3 (.Q(RG3_q));  // open: D, en, clk, clr
  Counter #(.width(4), .max('hf), .trigger("falling")) CT (.carry(CT_carry));  // open: load, D, count, Q, clk, clr
  // Probe on CT_carry
  Adder #(.width(9)) adder_1 (.a(RG1_q0), .b({RG3_q, bit_extender_1_out}), .out(adder_1_out));  // open: cin, cout
  Shift_Register #(.length(4), .trigger("falling")) RG1 (
    .in(RG2_out), .d0(adder_1_out[0]), .q0(RG1_q0[0]), .d1(adder_1_out[1]), .q1(RG1_q0[1]),
    .d2(adder_1_out[2]), .q2(RG1_q0[2]), .d3(adder_1_out[3]), .q3(RG1_q0[3]));  // open: shift, clk, out, load, clr
  Shift_Register #(.length(5), .trigger("falling")) RG2 (
    .out(RG2_out), .d0(adder_1_out[8]), .q0(RG1_q0[8]), .d1(adder_1_out[7]), .q1(RG1_q0[7]),
    .d2(adder_1_out[6]), .q2(RG1_q0[6]), .d3(adder_1_out[5]), .q3(RG1_q0[5]), .d4(adder_1_out[4]),
    .q4(RG1_q0[4]));  // open: shift, in, clk, load, clr
  // Probe on RG1_q0[8]

  // Notes on the sheet:
  //   SM
endmodule
