// Logisim project lab2.circ as structural Verilog: 1 circuit, main circuit main
module main (
  input  ST,
  input  R,
  input  [6:0] X,
  input  [6:0] Y,
  output [13:0] Z,
  output W_RG2,
  output SL_RG2,
  output W_CT,
  output plus_1_CT,
  output W_RG3,
  output W_RG1,
  output SL_RG1,
  output R_RG1
);

  wire and_1_out, and_2_out, and_3_out, bitselector_1_out, G_out, RG2_out, xor_1_out;
  wire [0:0] multiplexer_1_out;
  wire [2:0] CT_q, MCR_q_3;
  wire [3:0] MCR_CT_q, MCR_q;
  wire [4:0] RA_q;
  wire [5:0] MCR_q_2;
  wire [6:0] RG3_q;
  wire [13:0] adder_1_out, bit_extender_1_out;
  wire [15:0] rom_1_data;

  Clock #(.highDuration(2), .lowDuration(2)) G (.out(G_out));
  // Probe on MCR_q_2[5]
  Multiplexer #(.select(3), .disabled(0), .enable("false")) multiplexer_1 (
    .in0(1'b0), .in1(ST), .in2(RG2_out), .in3(and_3_out), .in4(1'b0), .in5(1'b0), .in6(1'b0), .in7(1'b1),
    .out(multiplexer_1_out[0]), .sel(MCR_q_3));
  and and_1 (and_1_out, ~bitselector_1_out, G_out);  // AND_Gate
  and and_2 (and_2_out, bitselector_1_out, G_out);
  Shift_Register #(.length(7), .trigger("falling")) RG2 (
    .shift(plus_1_CT), .in(1'b0), .clk(bitselector_1_out), .out(RG2_out), .load(R_RG1), .d0(X[0]), .d1(X[1]),
    .d2(X[2]), .d3(X[3]), .d4(X[4]), .d5(X[5]), .d6(X[6]));  // open: clr, q0, q1, q2, q3, q4, q5, q6
  Counter #(.width(3), .max('h7), .ongoal("stay"), .trigger("falling")) CT (
    .load(R_RG1), .D(3'b001), .count(plus_1_CT), .Q(CT_q), .clk(bitselector_1_out));  // open: carry, clr
  Register #(.width(7), .trigger("falling")) RG3 (.D(Y), .en(R_RG1), .Q(RG3_q), .clk(bitselector_1_out));  // open: clr
  Shift_Register #(.length(14), .trigger("falling")) RG1 (
    .shift(plus_1_CT), .in(1'b0), .clk(bitselector_1_out), .load(W_RG1), .clr(R_RG1), .d0(adder_1_out[0]),
    .q0(Z[0]), .d1(adder_1_out[1]), .q1(Z[1]), .d2(adder_1_out[2]), .q2(Z[2]), .d3(adder_1_out[3]),
    .q3(Z[3]), .d4(adder_1_out[4]), .q4(Z[4]), .d5(adder_1_out[5]), .q5(Z[5]), .d6(adder_1_out[6]),
    .q6(Z[6]), .d7(adder_1_out[7]), .q7(Z[7]), .d8(adder_1_out[8]), .q8(Z[8]), .d9(adder_1_out[9]),
    .q9(Z[9]), .d10(adder_1_out[10]), .q10(Z[10]), .d11(adder_1_out[11]), .q11(Z[11]), .d12(adder_1_out[12]),
    .q12(Z[12]), .d13(adder_1_out[13]), .q13(Z[13]));  // open: out
  Register #(.width(5), .trigger("high")) RA (
    .D({MCR_q, multiplexer_1_out[0]}), .en(and_1_out), .Q(RA_q), .clk(and_1_out), .clr(R));
  // Probe on RG2_out
  and and_3 (and_3_out, CT_q[0], CT_q[1], CT_q[2]);
  // Probe on and_3_out
  assign bit_extender_1_out = {{7{1'b0}}, RG3_q};  // Bit_Extender bit_extender_1
  ROM #(.addrWidth(5), .dataWidth(16)) rom_1 (.addr(RA_q), .data(rom_1_data), .sel(1'b1));
  Adder #(.width(14)) adder_1 (.a(bit_extender_1_out), .b(Z), .out(adder_1_out));  // open: cin, cout
  ExactlyOne xor_1 (
    .out(xor_1_out), .in0(rom_1_data[0]), .in1(rom_1_data[1]), .in2(rom_1_data[2]), .in3(rom_1_data[3]),
    .in4(rom_1_data[4]), .in5(rom_1_data[5]), .in6(rom_1_data[6]), .in7(rom_1_data[7]), .in8(rom_1_data[9]),
    .in9(rom_1_data[10]), .in10(rom_1_data[11]), .in11(rom_1_data[12]), .in12(rom_1_data[13]),
    .in13(rom_1_data[14]), .in14(rom_1_data[15]));
  // Probe on R_RG1
  // Probe on W_RG1
  // Probe on plus_1_CT
  // Probe on MCR_q_2[5]
  // Probe on xor_1_out
  Register #(.width(16), .trigger("falling")) MCR (
    .D(rom_1_data), .en(and_1_out), .Q({MCR_q, MCR_q_3, R_RG1, W_RG1, plus_1_CT, MCR_q_2}), .clk(G_out),
    .clr(R));
  Counter #(.width(4), .max('hf), .trigger("falling")) MCR_CT (
    .load(and_1_out), .D(rom_1_data[4:1]), .count(and_2_out), .Q(MCR_CT_q), .clk(G_out), .clr(R));  // open: carry
  BitSelector #(.width(4)) bitselector_1 (.in(MCR_CT_q), .out(bitselector_1_out), .sel(2'b11));

  assign SL_RG1 = plus_1_CT;
  assign SL_RG2 = plus_1_CT;
  assign W_CT = R_RG1;
  assign W_RG2 = R_RG1;
  assign W_RG3 = R_RG1;

  // Notes on the sheet:
  //   contents of rom_1 (hex, n*v repeats v):
  //   21f 151f 261f 1098 145e 303f 303f
endmodule
