// Logisim project mpcu.circ as structural Verilog: 1 circuit, main circuit main
module main (
  input  ST,
  input  RG2_0,
  input  CT_n,
  input  R
);

  wire and_1_out, and_2_out, bitselector_1_out, G_out, xor_1_out;
  wire [0:0] multiplexer_1_out;
  wire [2:0] MCR_q_3;
  wire [3:0] MCR_CT_q, MCR_q;
  wire [4:0] RA_q;
  wire [8:0] MCR_q_2;
  wire [15:0] rom_1_data;

  Clock #(.highDuration(2), .lowDuration(2)) G (.out(G_out));
  Multiplexer #(.select(3), .disabled(0), .enable("false")) multiplexer_1 (
    .in0(1'b0), .in1(ST), .in2(RG2_0), .in3(CT_n), .in4(1'b0), .in5(1'b0), .in6(1'b0), .in7(1'b1),
    .out(multiplexer_1_out[0]), .sel(MCR_q_3));
  and and_1 (and_1_out, ~bitselector_1_out, G_out);  // AND_Gate
  and and_2 (and_2_out, bitselector_1_out, G_out);
  Register #(.width(5), .trigger("high")) RA (
    .D({MCR_q, multiplexer_1_out[0]}), .en(and_1_out), .Q(RA_q), .clk(and_1_out), .clr(R));
  ROM #(.addrWidth(5), .dataWidth(16)) rom_1 (.addr(RA_q), .data(rom_1_data), .sel(1'b1));
  // Probe on xor_1_out
  ExactlyOne xor_1 (
    .out(xor_1_out), .in0(rom_1_data[0]), .in1(rom_1_data[1]), .in2(rom_1_data[2]), .in3(rom_1_data[3]),
    .in4(rom_1_data[4]), .in5(rom_1_data[5]), .in6(rom_1_data[6]), .in7(rom_1_data[7]), .in8(rom_1_data[9]),
    .in9(rom_1_data[10]), .in10(rom_1_data[11]), .in11(rom_1_data[12]), .in12(rom_1_data[13]),
    .in13(rom_1_data[14]), .in14(rom_1_data[15]));
  // Probe on MCR_q_2[8]
  // Probe on MCR_q_2[7]
  // Probe on MCR_q_2[6]
  // Probe on MCR_q_2[5]
  Register #(.width(16), .trigger("falling")) MCR (
    .D(rom_1_data), .en(and_1_out), .Q({MCR_q, MCR_q_3, MCR_q_2}), .clk(G_out), .clr(R));
  Counter #(.width(4), .max('hf), .trigger("falling")) MCR_CT (
    .load(and_1_out), .D(rom_1_data[4:1]), .count(and_2_out), .Q(MCR_CT_q), .clk(G_out), .clr(R));  // open: carry
  BitSelector #(.width(4)) bitselector_1 (.in(MCR_CT_q), .out(bitselector_1_out), .sel(2'b11));

  // Notes on the sheet:
  //   contents of rom_1 (hex, n*v repeats v):
  //   21f 151f 261f 1098 145e 303f 303f
endmodule
